// Logisim project 2_Lógica_Digital.circ as structural Verilog
module Ejercicio_12 (
  input  A,
  input  X,
  input  in_3,
  input  B
);

  wire and_1_out, clk_out, d_ff_1_qn, nor_1_out;

  nor nor_1 (nor_1_out, A, X);
  and and_1 (and_1_out, A, d_ff_1_qn);
  Clock clk (.out(clk_out));
  J_K_Flip_Flop j_k_ff_1 (.J(nor_1_out), .K(nor_1_out), .clk(clk_out), .Q(A), .Qn(in_3));  // open: preset, reset
  D_Flip_Flop d_ff_1 (.D(and_1_out), .clk(clk_out), .Q(B), .Qn(d_ff_1_qn));  // open: preset, reset
endmodule

module Ejercicio_13 (
  input  S0,
  input  E0,
  input  Q_T,
  input  S1,
  input  E1,
  input  in_6,
  input  S2,
  input  E2,
  input  in_9
);

  wire clk0_out, clk1_out, clk2_out, not_1_out, xor_1_out, xor_2_out, xor_3_out;

  xor xor_1 (xor_1_out, S0, E0);
  Clock clk0 (.out(clk0_out));
  Clock clk2 (.out(clk2_out));
  D_Flip_Flop d_ff_1 (.D(xor_1_out), .clk(clk0_out), .Q(S0), .Qn(Q_T));  // open: preset, reset
  J_K_Flip_Flop j_k_ff_1 (.J(xor_2_out), .K(E1), .clk(clk1_out), .Q(S1), .Qn(in_6));  // open: preset, reset
  xor xor_2 (xor_2_out, S1, E1);
  Clock clk1 (.out(clk1_out));
  J_K_Flip_Flop j_k_ff_2 (.J(xor_3_out), .K(E2), .clk(not_1_out), .Q(S2), .Qn(in_9));  // open: preset, reset
  xor xor_3 (xor_3_out, S2, E2);
  not not_1 (not_1_out, clk2_out);
endmodule

module Ejercicio_14 (
  input  i0,
  input  i1,
  input  i2,
  input  i3,
  input  load,
  output o0,
  output o1,
  output o2,
  output o3
);

  wire and_1_out, clk_out;

  Clock clk (.out(clk_out));
  D_Flip_Flop d_ff_1 (.D(i0), .clk(and_1_out), .Q(i0));  // open: Qn, preset, reset
  D_Flip_Flop d_ff_2 (.D(i1), .clk(and_1_out), .Q(i1));  // open: Qn, preset, reset
  D_Flip_Flop d_ff_3 (.D(i2), .clk(and_1_out), .Q(i2));  // open: Qn, preset, reset
  D_Flip_Flop d_ff_4 (.D(i3), .clk(and_1_out), .Q(i3));  // open: Qn, preset, reset
  and and_1 (and_1_out, load, clk_out);

  assign o0 = i0;
  assign o1 = i1;
  assign o2 = i2;
  assign o3 = i3;
endmodule

module Ejercicio_15 (
  input  d0,
  input  d1,
  input  d2,
  input  d3,
  input  load,
  input  read,
  output out_7,
  output out_8,
  output out_9,
  output out_10
);

  wire and_1_out, and_2_out, clk_out, d_ff_1_q, d_ff_2_q, d_ff_3_q, d_ff_4_q, not_1_out;

  Clock clk (.out(clk_out));
  not not_1 (not_1_out, read);
  and and_1 (and_1_out, clk_out, and_2_out);
  and and_2 (and_2_out, load, not_1_out);
  D_Flip_Flop d_ff_1 (.D(d0), .clk(and_1_out), .Q(d_ff_1_q));  // open: Qn, preset, reset
  D_Flip_Flop d_ff_2 (.D(d1), .clk(and_1_out), .Q(d_ff_2_q));  // open: Qn, preset, reset
  D_Flip_Flop d_ff_3 (.D(d2), .clk(and_1_out), .Q(d_ff_3_q));  // open: Qn, preset, reset
  D_Flip_Flop d_ff_4 (.D(d3), .clk(and_1_out), .Q(d_ff_4_q));  // open: Qn, preset, reset
  assign d0 = read ? d_ff_1_q : 1'bz;  // Controlled_Buffer controlled_buffer_1
  assign d1 = read ? d_ff_2_q : 1'bz;  // Controlled_Buffer controlled_buffer_2
  assign d2 = read ? d_ff_3_q : 1'bz;  // Controlled_Buffer controlled_buffer_3
  assign d3 = read ? d_ff_4_q : 1'bz;  // Controlled_Buffer controlled_buffer_4

  assign out_7 = d0;
  assign out_8 = d1;
  assign out_9 = d2;
  assign out_10 = d3;
endmodule
