// Logisim project Resolución.circ as structural Verilog: 8 circuits, main circuit Ejercicio1
module Ejercicio1 (
  input  Pulsador,
  input  Reset,
  output Q1,
  output Q0
);

  wire and_1_out, d_ff_2_qn;

  D_Flip_Flop d_ff_1 (.D(d_ff_2_qn), .clk(Pulsador), .Q(Q1), .reset(Reset));  // open: Qn, preset
  D_Flip_Flop d_ff_2 (.D(and_1_out), .clk(Pulsador), .Q(Q0), .Qn(d_ff_2_qn), .preset(Reset));  // open: reset
  and and_1 (and_1_out, d_ff_2_qn, Q1);
endmodule

module Ejercicio2 (
  input  Pulsador,
  output Q1,
  output Q0
);

  J_K_Flip_Flop j_k_ff_1 (.J(1'b1), .K(1'b1), .clk(Pulsador), .Q(Q0));  // open: Qn, preset, reset
  J_K_Flip_Flop j_k_ff_2 (.J(Q0), .K(Q0), .clk(Pulsador), .Q(Q1));  // open: Qn, preset, reset
endmodule

module Ejercicio3 (
  input  Pulsador,
  output Q1,
  output Q0
);

  wire ejercicio2_1_q0, ejercicio2_1_q1, not_1_out;

  Ejercicio2 ejercicio2_1 (.Pulsador(Pulsador), .Q1(ejercicio2_1_q1), .Q0(ejercicio2_1_q0));
  and and_1 (Q1, ejercicio2_1_q1, not_1_out);
  not not_1 (not_1_out, ejercicio2_1_q0);
  or or_1 (Q0, ejercicio2_1_q1, ejercicio2_1_q0);
endmodule

module Ejercicio3Bis (
  input  Pulsador,
  input  NEG,
  output Q1,
  output Q0
);

  wire ejercicio3_1_q0, ejercicio3_1_q1;

  Ejercicio3 ejercicio3_1 (.Pulsador(Pulsador), .Q1(ejercicio3_1_q1), .Q0(ejercicio3_1_q0));
  xor xor_1 (Q1, ejercicio3_1_q1, NEG);
  xor xor_2 (Q0, ejercicio3_1_q0, NEG);
endmodule

module Ej4 (
  input  B1,
  input  B0,
  output Q1,
  output Q0
);

  wire xor_1_out;

  not not_1 (Q1, B1);
  xor xor_1 (xor_1_out, B1, B0);
  not not_2 (Q0, xor_1_out);
endmodule

module Ej1V2 (
  input  Pulsador,
  input  Reset,
  output Q1,
  output Q0
);

  wire ejercicio1_1_q0, ejercicio1_1_q1;

  Ejercicio1 ejercicio1_1 (.Pulsador(Pulsador), .Reset(Reset), .Q1(ejercicio1_1_q1), .Q0(ejercicio1_1_q0));
  Ej4 ej4_1 (.B1(ejercicio1_1_q1), .B0(ejercicio1_1_q0), .Q1(Q1), .Q0(Q0));
endmodule

module Ej3V2 (
  input  Pulsador,
  output Q1,
  output Q0
);

  wire ejercicio3_1_q0, ejercicio3_1_q1;

  Ejercicio3 ejercicio3_1 (.Pulsador(Pulsador), .Q1(ejercicio3_1_q1), .Q0(ejercicio3_1_q0));
  Ej4 ej4_1 (.B1(ejercicio3_1_q1), .B0(ejercicio3_1_q0), .Q1(Q1), .Q0(Q0));
endmodule

module Ej3BisV2 (
  input  Pulsador,
  input  NEG,
  output Q1,
  output Q0
);

  wire ejercicio3bis_1_q0, ejercicio3bis_1_q1;

  Ejercicio3Bis ejercicio3bis_1 (.Pulsador(Pulsador), .NEG(NEG), .Q1(ejercicio3bis_1_q1), .Q0(ejercicio3bis_1_q0));
  Ej4 ej4_1 (.B1(ejercicio3bis_1_q1), .B0(ejercicio3bis_1_q0), .Q1(Q1), .Q0(Q0));
endmodule
